# Fritzing sketch DHT22_LCD_I2C (saved by Fritzing 0.9.3b)
circuit board: 10.5759cm x 5.71717cm
breadboards: 1

parts:
  LCM1602_IIC1 = LCM1602 IIC [part_number="LCM1602 IIC" chip_label="LCM1602 IIC" package="DIP (Dual Inline) [THT]"]
  LCD1 = LCD screen
  Part1 = Arduino Nano (Rev3.0)
  RHT1 = Humidity and Temperature Sensor RHT03 [part_number=DHT22]
  U2 = LIPO-1000mAh [package=lipo-1000]  # not connected

nets (from the pcb view):
  VSS: LCM1602_IIC1.VSS, LCM1602_IIC1.VDD, LCM1602_IIC1.V0, LCM1602_IIC1.RS, LCM1602_IIC1.E, LCM1602_IIC1.D0, LCM1602_IIC1.D1, LCM1602_IIC1.D2, LCM1602_IIC1.D3, LCM1602_IIC1.D5, LCM1602_IIC1.D6, LCM1602_IIC1.D7, LCM1602_IIC1.A, LCM1602_IIC1.K, LCD1.VSS, LCD1.VDD, LCD1.V0, LCD1.RS, LCD1.E, LCD1.DB0, LCD1.DB1, LCD1.DB2, LCD1.DB3, LCD1.DB5, LCD1.DB6, LCD1.DB7, LCD1.LED+, LCD1.LED-
  N1: LCM1602_IIC1.RW, LCD1.R/W
  N2: LCM1602_IIC1.D4, LCD1.DB4
  GND: LCM1602_IIC1.GND, Part1.GND, RHT1.GND_2
  VCC: LCM1602_IIC1.VCC, Part1.5V
  N3: LCM1602_IIC1.SDA, Part1.A4
  N4: LCM1602_IIC1.SCL, Part1.A5
  N5: LCM1602_IIC1.LED_A, LCM1602_IIC1.LED_B
  N6: Part1.D9, RHT1.Data-signal
  3V3: Part1.3V3, RHT1.Vcc

notes:
  DHT22

custom parts:
  LCM1602 IIC: I2C-Module to use a 1602 or 2004 LCD on with the wire.h libory Serial LCD Modul

// code stored in the sketch: AnalogReadSerial2LCD_LED.ino
#include <Wire.h>
#include <LiquidCrystal_I2C.h>

LiquidCrystal_I2C lcd(0x27, 16, 2);   // adress and format LCD

const int analogInPin = A0;           // Analog input pin that the potentiometer is attached to
const int analogOutPin = 9;           // Analog output pin that the LED is attached to

int sensorValue = 0;                  // value read from the pot
int outputValue = 0;                  // value output to the PWM (analog out)

void setup() {
  lcd.init();                         // init LCD
  lcd.backlight();
  lcd.home();
  lcd.setCursor(5, 0);                // place static text
  lcd.print("ADC = ");
  lcd.setCursor(15, 0);
  lcd.print("V");
  lcd.setCursor(0, 1);
  lcd.print("LED : ");
  lcd.setCursor(12, 1);
  lcd.print("%");
  Serial.begin(9600);                 // optional serial monitor
}

void loop() {
  int sensorValue = analogRead(analogInPin);          // read analog A0 en store in sensorValue
  float voltValue = 5.0 / 1024.0 * sensorValue;       // calculate volt at analog A0 and store in voltValue
  float percentValue = sensorValue / 1024.0 * 100.0;  // calculate percentage analog A0 and store in percentValue
  outputValue = map(sensorValue, 0, 1023, 0, 255);    // map analog input to analog output and store in outputValue
  analogWrite(analogOutPin, outputValue);             // write outputValue to analogOutPin

  lcd.setCursor(0, 0);                                // set cursor at deserid position
  leadingZeros(sensorValue, 4);                       // print sensorvalue with number of leading-characters (0 or space as specified in function leadingZeros)
  lcd.setCursor(10, 0);                               // set cursor at deserid position
  lcd.print(voltValue);                               // print voltValue
  lcd.setCursor(6, 1);                                // set cursor at deserid position
  lcd.print(percentValue);                            // print percentValue

  Serial.print("sensor = " );                         // print the results to the serial monitor:
  Serial.print(sensorValue);
  Serial.print("\t output = ");
  Serial.print(outputValue);
  Serial.print("\t procent = ");
  Serial.println(percentValue);

  delay(1000);                                        // set delay
}

void leadingZeros( int value, int width) {            // display result with leading characters
  char valueStr[6];                                   // large enough to hold an int
  itoa (value, valueStr, 10);                         // itoa converts int to string
  int len = strlen(valueStr);                         // calculate length of valueStr
  if (len < width) {
    len = width - len;
    while (len--)
      lcd.print(' ');                                 // for leading zeros place '0' between (), for leading spaces place ' ' between ()
  }
  lcd.print(valueStr);
}
