# Fritzing sketch Untitled Sketch (saved by Fritzing 0.9.3b)
breadboards: 1

parts:
  BMP280_Breakout1 = BMP280 Breakout Board [part_number=BMP280]
  Part1 = Arduino Uno (Rev3) - ICSP
  Part2 = Arduino Uno (Rev3) - ICSP
  Part3 = Soil Moisture Sensor
  Part4 = Humidity Sensor - HIH-4030 Breakout  # not connected

nets:
  VCC: BMP280_Breakout1.VCC, Part1.3V3
  GND: BMP280_Breakout1.GND, Part1.GND
  N1: BMP280_Breakout1.SCL, Part1.A5/SCL
  N2: BMP280_Breakout1.SDA, Part1.A4/SDA
  N3: Part2.A0, Part3.SIG
  5V: Part2.5V, Part3.VCC
  GND_2: Part2.GND, Part3.GND

custom parts:
  BMP280 Breakout Board: This is a breakout board for the Bosch Sensortec BMP280, "an absolute barometric pressure sensor especially designed for mobile applications." The operation range is 300 to 1100 hPa. Supply voltage is 1.2 to 3.6V. Operating temperature range is -40 to +85 °C.
