# Fritzing sketch moisture_serial_fritzing (saved by Fritzing 0.9.3b)
breadboards: 1

parts:
  부품1 = FC-28 Soil Hygrometer Module - Probe
  부품2 = FC-28 Soil Hygrometer Module
  부품3 = Arduino Uno (Rev3)
  BMP280_Breakout1 = BMP280 Breakout Board [part_number=BMP280]
  RHT1 = Humidity and Temperature Sensor RHT03
  KY-3 = Keyes Relay [package=THT]
  Grove1 = Grove Light Sensor

nets:
  N1: 부품1.POS, 부품2.POS
  N2: 부품1.NEG, 부품2.NEG
  VCC: 부품2.VCC, 부품3.5V, BMP280_Breakout1.VCC, RHT1.Vcc, KY-3.power, Grove1.VCC
  GND: 부품2.GND, 부품3.GND, BMP280_Breakout1.GND, RHT1.GND_2, KY-3.ground, Grove1.GND
  N3: 부품2.AO, 부품3.A0
  N4: 부품3.A4/SDA, BMP280_Breakout1.SDA
  N5: 부품3.A5/SCL, BMP280_Breakout1.SCL
  N6: 부품3.D2, RHT1.Data-signal, RHT1.GND_1
  N7: 부품3.D5_PWM, Grove1.SIG
  N8: 부품3.D6_PWM, KY-3.signal

notes:
  Soil sensor
  Light Sensor
  BMP280
  DHT22
  Pump

custom parts:
  FC-28 Soil Hygrometer Module - Probe: The FC-28 is a soil hygrometer module that uses the Texas Instruments LM393 comparator chip to provide an analog measurement of soil humidity.
  FC-28 Soil Hygrometer Module: The FC-28 is a soil hygrometer module that uses the Texas Instruments LM393 comparator chip to provide an analog measurement of soil humidity. The digital output is high when soil moisture is over a certain threshold, as determined by adjusting the potentiometer.
  BMP280 Breakout Board: This is a breakout board for the Bosch Sensortec BMP280, "an absolute barometric pressure sensor especially designed for mobile applications." The operation range is 300 to 1100 hPa. Supply voltage is 1.2 to 3.6V. Operating temperature range is -40 to +85 °C.
  Keyes Relay: The Keyes 5V relay module is suitable for SCM development, home appliance control. It uses a 5V~12V TIL control signal which can control DC / AC signal.
