# Fritzing sketch water and hand sanitizer dispenser (saved by Fritzing 0.8.7b)
breadboards: 1

parts:
  Part1 = Arduino Uno (Rev3)
  Part2 = Breakout Board for Electret Microphone
  J1 = Basic Servo
  Part3 = SRF05 Ultrasonic Rangefinder
  KY-2 = Keyes Relay [package=THT]
  M1 = DC Motor

nets:
  N1: Part1.A2, Part2.AUD
  N2: Part1.D3_PWM, J1.pulse
  N3: Part1.D4, Part3.Echo
  N4: Part1.D5_PWM, Part3.Trig
  VCC: Part1.5V, Part2.VCC, J1.vcc, Part3.VCC, KY-2.C
  GND: Part1.GND, Part2.GND, J1.gnd, Part3.GND, M1.pin_2
  N5: KY-2.NO, M1.pin_1

notes:
  Relay
  Ultrasonic HC-SR04
  Water Pump
  Sound Sensor
  Servo

custom parts:
  Keyes Relay: The Keyes 5V relay module is suitable for SCM development, home appliance control. It uses a 5V~12V TIL control signal which can control DC / AC signal.
